# Fritzing sketch dooropener3 (saved by Fritzing 0.9.2b)
circuit board: 6.81769cm x 5.95483cm

parts:
  S1 = Toggle Switch [package=THT]
  J1 = Screw terminal - 2 pins [package=THT]
  C1 = Electrolytic Capacitor [capacitance=10µF package="100 mil [THT, electrolytic]"]
  C2 = Electrolytic Capacitor [capacitance=10µF package="100 mil [THT, electrolytic]"]
  LED1 = LED - 3mm [color="Red (633nm)" package="3 mm [THT]"]
  R1 = Resistor [tolerance=±5% resistance=330 package="2010 [SMD]"]
  XTAL1 = CRYSTAL - kHz [frequency="16 MHz"]
  C3 = Ceramic Capacitor [capacitance=22pF package="100 mil [THT, multilayer]"]
  C4 = Ceramic Capacitor [capacitance=22pF package="100 mil [THT, multilayer]"]
  R2 = Resistor [tolerance=±5% resistance=10k package=THT]
  C5 = Electrolytic Capacitor [capacitance=10µF package="100 mil [THT, electrolytic]"]
  IC1 = Voltage Regulator [package=to220-igo]
  U1 = atmega168 [package=dip]
  MD09B1 = A4988 Stepper Motor Driver Carrier
  J2 = Screw terminal - 2 pins [package=THT]
  J3 = Screw terminal - 2 pins [package=THT]
  J4 = Screw terminal - 2 pins [package=THT]
  C6 = Electrolytic Capacitor [capacitance=1µF package="100 mil [THT, electrolytic]"]
  U2 = Voltage Regulator - 3.3V [package="TO220 [THT]"]
  Part1 = RFID-RC522-v2

nets:
  GND: S1.L1, J1.pin1, C1.-, C2.-, LED1.cathode, C3.1, C4.1, IC1.GND, U1.GND, U2.GND, Part1.GND
  N1: S1.COM, C5.+, U1.RESET
  N2: S1.L2, R2.Pin_0
  N3: J1.pin2, C1.+, IC1.IN, U2.input_voltage
  VCC: C2.+, R1.Pin_0, R2.Pin_1, IC1.OUT, U1.VCC, U1.AVCC, U1.AREF, MD09B1.VDD
  N4: LED1.anode, R1.Pin_1
  N5: XTAL1.pin_0, C3.0, U1.XLAT2
  N6: XTAL1.pin_1, C4.0, U1.XLAT1
  N7: U1.D9_(PWM), Part1.RST
  N8: U1.D10_(PWM), Part1.SDA
  N9: U1.D11_(PWM), Part1.MOSI
  N10: U1.D12, Part1.MISO
  N11: U1.D13, Part1.SCK
  N12: MD09B1.RESET, MD09B1.SLEEP
  N13: MD09B1.STEP, MD09B1.DIR, MD09B1.GROUND#147
  N14: MD09B1.VMOT, J2.pin1, C6.+
  N15: MD09B1.GROUND#141, J2.pin2, C6.-
  N16: MD09B1.OUT_2B, J3.pin1
  N17: MD09B1.OUT_2A, J3.pin2
  N18: MD09B1.OUT_1A, J4.pin1
  N19: MD09B1.OUT_1B, J4.pin2
  N20: U2.output_voltage, Part1.3_3V

custom parts:
  RFID-RC522-v2: A simple China made RFID-RC522 Reader; do check the pin labels, as this is a MFRC522 based clone.
